# Fritzing sketch OneWireBreadboard (saved by Fritzing 0.9.4)
breadboards: 1

parts:
  Q1 = NPN-Transistor [package="TO92 [THT]"]
  Q2 = NPN-Transistor [package="TO92 [THT]"]
  R1 = Resistor [tolerance=±5% resistance=100k package="0603 [SMD]"]
  R2 = Resistor [tolerance=±5% resistance=4.7k package=THT]
  R3 = Resistor [tolerance=±5% resistance=680 package=THT]

nets:
  N1: Q1.E, Q2.E
  N2: Q1.C, Q2.B, R1.Pin_0
  N3: Q2.C, R2.Pin_0, R3.Pin_0
  N4: R1.Pin_1, R2.Pin_1
